// Logisim project Inversor_de_3_bits.circ as structural Verilog: 1 circuit, main circuit main
module main (
  input  [2:0] e0__e1__e2,
  input  e3,
  output [2:0] s0__s1__s2
);

  xor xor_1 (s0__s1__s2[0], e0__e1__e2[0], e3);
  xor xor_2 (s0__s1__s2[1], e0__e1__e2[1], e3);
  xor xor_3 (s0__s1__s2[2], e0__e1__e2[2], e3);
endmodule
