// Logisim project Sumador_Completo.circ as structural Verilog: 1 circuit, main circuit main
module main (
  input  B,
  input  A,
  input  C_in,
  output C_out,
  output Sum
);

  wire and_1_out, and_2_out, xor_1_out;

  or or_1 (C_out, and_1_out, and_2_out);
  and and_1 (and_1_out, B, A);
  and and_2 (and_2_out, xor_1_out, C_in);
  xor xor_1 (xor_1_out, B, A);
  xor xor_2 (Sum, xor_1_out, C_in);
endmodule
