// Logisim project combinacionales.circ as structural Verilog: 11 circuits, main circuit verificador
module sumador_simple (
  input  A,
  input  B,
  output S,
  output Cout
);
endmodule

module sumador_completo (
  input  Cin,
  input  A,
  input  B,
  output S,
  output Cout
);
endmodule

module sumador_4 (
  input  Cin,
  input  [3:0] A,
  input  [3:0] B,
  output [3:0] S,
  output Cout
);

  Hex_Digit_Display hex_digit_display_1 (.value(S));  // open: dp
endmodule

module comparador_cero (
  input  [3:0] A,
  output Z
);
endmodule

module sumador_flags (
  input  Cin,
  input  [3:0] A,
  input  [3:0] B,
  output [3:0] S,
  output N,
  output Z,
  output V,
  output C
);

  Hex_Digit_Display hex_digit_display_1 (.value(S));  // open: dp
  comp_overflow comp_overflow_1 ();  // open: c3, a3, b3, O
endmodule

module incrementador_4 (
  input  [3:0] A,
  output [3:0] S
);

  sumador_4 sumador_4_1 (.A(A), .B(4'b0001), .S(S));  // open: Cin, Cout
  Hex_Digit_Display hex_digit_display_1 (.value(S));  // open: dp
endmodule

module inversor_4 (
  input  [3:0] A,
  input  INV,
  output [3:0] S
);

  wire [3:0] incrementador_4_1_s, not_1_out;

  not not_1 (not_1_out[0], A[0]);
  not not_2 (not_1_out[1], A[1]);
  not not_3 (not_1_out[2], A[2]);
  not not_4 (not_1_out[3], A[3]);
  Multiplexer #(.width(4)) multiplexer_1 (.in0(A), .in1(incrementador_4_1_s), .out(S), .sel(INV));
  incrementador_4 incrementador_4_1 (.A(not_1_out), .S(incrementador_4_1_s));
  Hex_Digit_Display hex_digit_display_1 (.value(S));  // open: dp
endmodule

module ALU (
  input  [3:0] A,
  input  [3:0] B,
  input  [1:0] OP,
  output N,
  output Z,
  output V,
  output C,
  output [3:0] S
);

  inversor_4 inversor_4_1 (.A(B));  // open: INV, S
  overflow_resta overflow_resta_1 (.B(B));  // open: V_in, V_out
  Hex_Digit_Display hex_digit_display_1 (.value(S));  // open: dp
endmodule

module verificador (
  output [3:0] out_1,
  output [3:0] out_2,
  output [1:0] out_3,
  output halt,
  output N,
  output Z,
  output V,
  output C,
  output [3:0] res
);

  wire clock_1_out;

  Clock clock_1 (.out(clock_1_out));
  Counter #(.max('h3ff), .width(10)) counter_1 (
    .clk(clock_1_out), .carry(halt), .Q({out_3, out_2, out_1}));  // open: clr, load, up, count, D
  ALU alu_1 (.A(out_1), .B(out_2), .OP(out_3), .N(N), .Z(Z), .V(V), .C(C), .S(res));
endmodule

module overflow_resta (
  input  V_in,
  input  [3:0] B,
  output V_out
);

  wire comparador_cero_1_z, not_2_out;
  wire [3:3] not_1_out;

  not not_1 (not_1_out[3], B[3]);
  not not_2 (not_2_out, V_in);
  comparador_cero comparador_cero_1 (.A({not_1_out[3], B[2:0]}), .Z(comparador_cero_1_z));
  Multiplexer multiplexer_1 (.in0(V_in), .in1(not_2_out), .out(V_out), .sel(comparador_cero_1_z));
endmodule

module comp_overflow (
  input  c3,
  input  a3,
  input  b3,
  output O
);

  wire not_1_out, xor_1_out, xor_2_out;

  xor xor_1 (xor_1_out, c3, a3);
  not not_1 (not_1_out, xor_2_out);
  xor xor_2 (xor_2_out, a3, b3);
  and and_1 (O, xor_1_out, not_1_out);
endmodule
